# Fritzing sketch Semenzaio Smart (saved by Fritzing 1.0.1rc)
breadboards: 1

parts:
  A1 = Arduino UNO R4 WiFi
  R1 = PHOTOCELL [package=photocell-kit]
  R2 = Resistor [tolerance=±5% resistance=220 package="0603 [SMD]"]
  Mod1 = KY-015 Temperature & Humidity Sensor Module [package="Breakout board"]
  Componente1 = FC-28 Soil Hygrometer Module - Probe
  Componente2 = FC-28 Soil Hygrometer Module
  U1 = Module 4 Relais 5V [package="Module 4 Relais 5V"]
  220_V = Lilypad Battery Connect  # not connected
  LED1 = LEDs [package=led10mm]
  WATER_PUMP1 = water pump/motor  # not connected
  R3 = Heating Pad
  F1 = Fan - Ventilador [package=THT]
  U2 = Transformer [package=transformer]

nets:
  GND: A1.Pin_2, A1.Pin_10, A1.Pin_18, A1.Pin_30, A1.Pin_48, R2.Pin_1, Mod1.-, Componente2.GND, U1.GND
  N1: A1.Pin_7, A1.Pin_19, Mod1.Vin
  N2: A1.Pin_8, A1.Pin_27, R1.P$2, Componente2.VCC
  N3: A1.Pin_13, Componente2.AO
  N4: A1.Pin_36, Mod1.S
  N5: A1.Pin_37, U1.IN2
  N6: A1.Pin_38, U1.IN4
  N7: A1.Pin_39, U1.IN3
  N8: A1.Pin_40, U1.IN1
  N9: R1.P$1, R2.Pin_0
  N10: Componente1.POS, Componente2.POS
  N11: Componente1.NEG, Componente2.NEG
  N12: U1.K1-NF, U2.4
  N13: U1.K2-NF, R3.pin_1
  N14: U1.K4-NF, LED1.C
  N15: U1.K1-NO, F1.GND
  N16: U1.K3-NO, U1.K4-NO
  N17: F1.5V, U2.1

notes:
  Differenziale

custom parts:
  Arduino UNO R4 WiFi: The Arduino UNO R4 WiFi merges the RA4M1 microprocessor from Renesas with the ESP32-S3 from Espressif, creating an all-in-one tool for makers with enhanced processing power and a diverse array of new peripherals.
  KY-015 Temperature & Humidity Sensor Module: KY-015 temperature and humidity sensor module, provides a low-latency serial interface to measure humidity and temperature.
  FC-28 Soil Hygrometer Module - Probe: The FC-28 is a soil hygrometer module that uses the Texas Instruments LM393 comparator chip to provide an analog measurement of soil humidity.
  FC-28 Soil Hygrometer Module: The FC-28 is a soil hygrometer module that uses the Texas Instruments LM393 comparator chip to provide an analog measurement of soil humidity. The digital output is high when soil moisture is over a certain threshold, as determined by adjusting the potentiometer.
  Module 4 Relais 5V: Module 4 Relais 5V 4x SPD-06VDC-SD-C
  LEDs: LEDs Standard schematic elements and footprints for 5mm, 3mm, 1206, and 0603 sized LEDs. 5mm - Spark Fun Electronics SKU : COM-00529 (and others)
  water pump/motor: WATER PUMP BY ARDUBLOCKTR
  Heating Pad: A thermoresistant material with an embeded conductor that dissipates electrical energy into heat.
  Fan - Ventilador: Ventilador de 2 pines, se encuentra comunmente en computadoras de escritorio
